# Fritzing sketch circuit_fritzing (saved by Fritzing 0.9.3b)
breadboards: 1

parts:
  U2 = LCD-16X2 [package=lcd-16x2_noholes]
  M1 = 1 chan 5v relay module
  Part3 = RFID-RC522-v2
  VALVE1 = Plastic Solenoid Valve
  Power_plug1 = Power plug
  Part4 = Arduino Uno (Rev3)

nets:
  VSS: U2.VSS, U2.R_W, U2.K, M1.pin_2, Part3.MOSI, Part4.GND
  VDD: U2.VDD, U2.A, M1.pin_1, Part4.5V
  N1: U2.VO, Part4.D6_PWM
  N2: U2.RS, Part4.D8
  N3: U2.E, Part4.D7
  N4: U2.DB4, Part4.D5_PWM
  N5: U2.DB5, Part4.D4
  N6: U2.DB6, Part4.D3_PWM
  N7: U2.DB7, Part4.D2
  N8: M1.pin_3, Part4.D1/TX
  N9: M1.pin_4, Power_plug1.VCC
  N10: M1.pin_5, VALVE1.no_name_yet#2
  N11: Part3.SDA, Part4.3V3
  N12: Part3.SCK, Part4.D9_PWM
  N13: Part3.IRQ, Part4.D12/MISO
  N14: Part3.GND, Part4.D11_PWM/MOSI
  N15: Part3.RST, Part4.D13/SCK
  N16: Part3.3_3V, Part4.D10_PWM/SS
  N17: VALVE1.no_name_yet#1, Power_plug1.GND

custom parts:
  1 chan 5v relay module: 1 Channel 5V Relay Module Board Shield with Optocoupler Support High and Low Level Trigger for Arduino.
  RFID-RC522-v2: A simple China made RFID-RC522 Reader; do check the pin labels, as this is a MFRC522 based clone.
